# Fritzing sketch wireless_weather_station (saved by Fritzing 0.9.3b)
breadboards: 1

parts:
  Componente1 = Arduino Mega 2560 (Rev3)
  ZS-042_RTC1 = ZS-042 RTC Module  # not connected
  Componente2 = Barometric Pressure Sensor - BMP180 Breakout (GY-68)

nets:
  N1: Componente1.D11_PWM, Componente2.SDA
  N2: Componente1.D10_PWM, Componente2.SCL
  3V3: Componente1.3V3, Componente2.VCC
  GND: Componente1.GND, Componente2.GND

// code stored in the sketch: Code.ino
//#include <Whire.h>
#include <SFE_BMP180.h> //Library for pressure sensor
#define SCL_BMP180 10 //pressure sensor pin
#define SDA_BMP180 11 //pressure sensor pin

double temperature;
double pressure;

SFE_BMP180 bmp180; //Initializing pressure sensor

void setup() {
  
  Serial.begin(9600);
  initializeBmp180();
  
}

void loop() {

  readTemperaturePressure();
  
}

void initializeBmp180(){
  Serial.println(bmp180.begin());
  if (bmp180.begin()){
    Serial.println("BMP180 initialize correctly");
  } else {
    Serial.println("Fail to initialize BMP180");
    delay(2000);
    initializeBmp180();
  }
}

void readTemperaturePressure(){

  char status;
  double T,P;

  status = bmp180.startTemperature();//Init to read temperature
  if (status != 0)
  {   
    delay(status); //Stop to finalize read
    status = bmp180.getTemperature(T); //Get Temperature
    if (status != 0)
    {
      status = bmp180.startPressure(3); //Init to read pressure
      if (status != 0)
      {        
        delay(status);//Stop to finalize read      
        status = bmp180.getPressure(P,T); //Get pressure
        if (status != 0)
        {                  
          Serial.print("Temperature: ");
          Serial.print(T,2);
          Serial.print(" °C , ");
          Serial.print("Pressure: ");
          Serial.print(P,2);
          Serial.println(" mb");  
          
          //pressure = P;
          
          if (P < 1025)
          {
            analogWrite(SCL_BMP180, 250);
            Serial.println("Presión baja");
            delay(2150);
            digitalWrite(SCL_BMP180, LOW);
            delay(2150);
          } else
          {
            analogWrite(SDA_BMP180, 250);
            Serial.println("Presión alta");
            delay(1000);
            digitalWrite(SDA_BMP180, LOW);
            delay(1000);
          }
          
        }      
      }      
    }   
  } 
  delay(1000);

}
